# Fritzing sketch arduinoISP (saved by Fritzing 0.6.3b)
breadboards: 1

parts:
  U1 = atmega168 [package="DIP28 [THT]"]
  S1 = Pushbutton [package=THT]
  R1 = Resistor [tolerance=±5% resistance=220 package=THT]
  LED1 = LED - 5mm [color="Red (633nm)" package="5 mm [THT]"]
  R2 = Resistor [tolerance=±5% resistance=10k package=THT]
  Arduino1 = Arduino
  R3 = Resistor [tolerance=±5% resistance=120 package=THT]

nets:
  N1: U1.Pin_1, S1.leg1, R2.Pin_1, Arduino1.D10
  5V: U1.Pin_7, U1.Pin_20, R2.Pin_0, Arduino1.+5V, R3.Pin_0
  GND: U1.Pin_8, U1.Pin_22, R1.Pin_0, Arduino1.GND
  N2: U1.Pin_15, LED1.anode
  N3: U1.Pin_17, Arduino1.D11
  N4: U1.Pin_18, Arduino1.D12
  N5: U1.Pin_19, Arduino1.D13
  N6: R1.Pin_1, LED1.cathode
  N7: Arduino1.RST, R3.Pin_1

notes:
  Wiederstand zum Reset bei DCD verhindern
